# Fritzing sketch frog_sensor (saved by Fritzing 0.9.8b)

parts:
  MCU1 = Raspberry Pi Zero
  Part1 = Adafruit SCD30 [part_number="Adafruit #4867"]
  Part2 = Adafruit DPS310 Precision Barometric Pressure and Altitude Sensor [part_number="Adafruit #4494"]
  M1 = bb-usb-cable [package=THT]  # not connected
  U1 = SUP500F [package=sup500f]  # not connected

nets:
  VCC: MCU1.pin_2, MCU1.pin_4, Part1.VCC, Part2.VCC
  N1: MCU1.pin_3, Part1.SDA, Part2.SDI/SDA
  N2: MCU1.pin_5, Part1.SCL, Part2.SCK/SCL
  GND: MCU1.pin_6, Part1.GND, Part2.GND

custom parts:
  Adafruit DPS310 Precision Barometric Pressure and Altitude Sensor: How high are you right now? If you had a precision altitude sensor, you would know for sure! The DPS310 sensor from Infineon a high precision barometric sensor, perfect for measuring altitude changes with a up to ±0.002 hPa (or ±0.02 m) precision high precision mode and ± 1 hPa absolute accuracy. That means you can know your absolute altitude with 1 meter accuracy when you set the sea-level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
  bb-usb-cable: Breadboard only, no connectors USB cable for the Raspberry PIs.
